// Logisim project PorteLogiqueNON.circ as structural Verilog: 1 circuit, main circuit main
module main (
  input  in_1,
  input  in_2,
  input  in_3,
  input  in_4,
  input  in_5,
  input  in_6,
  input  in_7,
  input  in_8,
  input  in_9,
  input  in_10,
  output out_11,
  output out_12,
  output out_13,
  output out_14,
  output out_15,
  output out_16
);

  wire transistor_3_out, transistor_6_out, transistor_9_out, transistor_10_out;

  Transistor transistor_1 (.in(1'b1), .out(out_12), .gate(in_3));
  Transistor #(.\type ("n")) transistor_2 (.in(1'b0), .out(out_12), .gate(in_3));
  not not_1 (out_14, in_8);
  Transistor transistor_3 (.in(1'b1), .out(transistor_3_out), .gate(in_4));
  Transistor transistor_4 (.in(1'b1), .out(transistor_3_out), .gate(in_5));
  Transistor #(.\type ("n")) transistor_5 (.in(transistor_6_out), .out(transistor_3_out), .gate(in_4));
  Transistor #(.\type ("n")) transistor_6 (.in(1'b0), .out(transistor_6_out), .gate(in_5));
  and and_1 (out_15, in_6, in_9);
  Transistor transistor_7 (.in(1'b1), .out(out_11), .gate(transistor_3_out));
  Transistor #(.\type ("n")) transistor_8 (.in(1'b0), .out(out_11), .gate(transistor_3_out));
  Transistor transistor_9 (.in(1'b1), .out(transistor_9_out), .gate(in_1));
  Transistor transistor_10 (.in(transistor_9_out), .out(transistor_10_out), .gate(in_2));
  Transistor #(.\type ("n")) transistor_11 (.in(1'b0), .out(transistor_10_out), .gate(in_2));
  Transistor #(.\type ("n")) transistor_12 (.in(1'b0), .out(transistor_10_out), .gate(in_1));
  or or_1 (out_16, in_7, in_10);
  Transistor transistor_13 (.in(1'b1), .out(out_13), .gate(transistor_10_out));
  Transistor #(.\type ("n")) transistor_14 (.in(1'b0), .out(out_13), .gate(transistor_10_out));

  // Notes on the sheet:
  //   Porte logique NON
  //   Porte logique ET
  //   Porte logique OU
endmodule
