// Logisim project Portes.circ as structural Verilog: 1 circuit, main circuit main
module main (
  input  A,
  input  in_2,
  input  B,
  input  in_4,
  input  A_2,
  input  A_3,
  input  A_4,
  input  B_2,
  input  B_3,
  input  A_5,
  input  B_4,
  input  C,
  output out_13,
  output out_14,
  output out_15,
  output out_16,
  output out_17,
  output out_18
);

  wire and_2_out, not_1_out, not_2_out, or_2_out;

  not not_1 (not_1_out, A);
  and and_1 (out_13, not_1_out, not_2_out);
  not not_2 (not_2_out, B);
  not not_3 (out_15, A_2);
  and and_2 (and_2_out, A_5, B_4);
  or or_1 (out_18, and_2_out, C);
  and and_3 (out_16, A_3, B_2);
  or or_2 (or_2_out, in_2, in_4);
  not not_4 (out_14, or_2_out);
  or or_3 (out_17, A_4, B_3);
endmodule
