// Logisim project nand.circ as structural Verilog: 1 circuit, main circuit main
module main (
  input  in_1,
  input  in_2,
  input  in_3,
  input  in_4,
  input  in_5,
  input  in_6,
  output out_7,
  output out_8,
  output out_9
);

  wire nand_1_out, nand_2_out, transistor_4_out;

  Transistor transistor_1 (.in(1'b1), .out(out_9), .gate(in_5));
  Transistor transistor_2 (.in(1'b1), .out(out_9), .gate(in_6));
  Transistor #(.\type ("n")) transistor_3 (.in(transistor_4_out), .out(out_9), .gate(in_5));
  Transistor #(.\type ("n")) transistor_4 (.in(1'b0), .out(transistor_4_out), .gate(in_6));
  nand nand_1 (nand_1_out, in_1, in_1);
  nand nand_2 (nand_2_out, in_4, in_4);
  nand nand_3 (out_7, nand_1_out, nand_2_out);
  nand nand_4 (out_8, in_2, in_3);
endmodule
