// Logisim project transistor.circ as structural Verilog: 1 circuit, main circuit main
module main (
  input  in_1,
  input  in_2,
  output out_3,
  output out_4
);

  wire transistor_2_out;

  Transistor transistor_1 (.in(1'b1), .out(out_3), .gate(in_1));
  Transistor #(.\type ("n")) transistor_2 (.in(out_3), .out(transistor_2_out), .gate(in_1));
  not not_1 (out_4, in_2);
  // also tied to GND on the sheet: transistor_2_out
endmodule
